# Fritzing sketch RoverUltrasonicSensorEvaluationUnit (saved by Fritzing 1.0.5)
circuit board: 8.46667cm x 5.64444cm
breadboards: 1

parts:
  Bauteil1 = Arduino Nano (Rev3.0) (ICSP)
  HC-SR04_Sensor_1 = HC-SR04 Ultrasonic Distance Sensor
  HC-SR04_Sensor_2 = HC-SR04 Ultrasonic Distance Sensor
  HC-SR04_Sensor_3 = HC-SR04 Ultrasonic Distance Sensor
  HC-SR04_Sensor_4 = HC-SR04 Ultrasonic Distance Sensor
  J1 = male pin header, 4 pins [form="♂ (male)"]
  J2 = male pin header, 4 pins [form="♂ (male)"]
  J3 = male pin header, 4 pins [form="♂ (male)"]
  J4 = male pin header, 4 pins [form="♂ (male)"]
  J5 = male pin header, 4 pins [form="♂ (male)"]

nets:
  GND: Bauteil1.GND, HC-SR04_Sensor_1.GND, HC-SR04_Sensor_2.GND, HC-SR04_Sensor_3.GND, HC-SR04_Sensor_4.GND, J1.pin4, J2.pin4, J3.pin4, J4.pin4, J5.pin3
  N1: Bauteil1.D3, HC-SR04_Sensor_4.ECHO, J4.pin3
  N2: Bauteil1.D4, HC-SR04_Sensor_1.TRIG, HC-SR04_Sensor_2.TRIG, HC-SR04_Sensor_3.TRIG, HC-SR04_Sensor_4.TRIG, J1.pin2, J2.pin2, J3.pin2, J4.pin2
  N3: Bauteil1.D5, HC-SR04_Sensor_3.ECHO, J3.pin3
  N4: Bauteil1.D6, HC-SR04_Sensor_2.ECHO, J2.pin3
  N5: Bauteil1.D9, HC-SR04_Sensor_1.ECHO, J1.pin3
  N6: Bauteil1.VIN, J5.pin4
  VCC: Bauteil1.5V, HC-SR04_Sensor_1.VCC, HC-SR04_Sensor_2.VCC, HC-SR04_Sensor_3.VCC, HC-SR04_Sensor_4.VCC, J1.pin1, J2.pin1, J3.pin1, J4.pin1
  N7: Bauteil1.A5, J5.pin2
  N8: Bauteil1.A4, J5.pin1

notes:
  i2c Bus + Power
